// Logisim project Somador de bits.circ as structural Verilog: 2 circuits, main circuit Somador de 2 bits
// SomaBIT
module Somador_de_2_bits (
  input  A,
  input  B,
  input  Cin,
  output coat,
  output s
);

  wire and_1_out, and_2_out, xor_2_out;

  or or_1 (coat, and_2_out, and_1_out);
  xor xor_1 (s, Cin, xor_2_out);
  and and_1 (and_1_out, Cin, xor_2_out);
  and and_2 (and_2_out, A, B);
  xor xor_2 (xor_2_out, A, B);
endmodule

module Somador_de_4_Bits (
  input  a1,
  input  b1,
  input  c1,
  input  d1,
  input  a2,
  input  b2,
  input  c3,
  input  d2,
  input  Co,
  output c4,
  output af,
  output bf,
  output cf,
  output df
);

  wire somador_de_2_bits_2_coat, somador_de_2_bits_3_coat, somador_de_2_bits_4_coat;

  Somador_de_2_bits somador_de_2_bits_1 (.coat(c4), .s(af), .A(a1), .B(a2), .Cin(somador_de_2_bits_2_coat));
  Somador_de_2_bits somador_de_2_bits_2 (
    .coat(somador_de_2_bits_2_coat), .s(bf), .A(b1), .B(b2), .Cin(somador_de_2_bits_3_coat));
  Somador_de_2_bits somador_de_2_bits_3 (
    .coat(somador_de_2_bits_3_coat), .s(cf), .A(c1), .B(c3), .Cin(somador_de_2_bits_4_coat));
  Somador_de_2_bits somador_de_2_bits_4 (.coat(somador_de_2_bits_4_coat), .s(df), .A(d1), .B(d2), .Cin(Co));
endmodule
