// Logisim project ULAversaofinal.circ as structural Verilog: 10 circuits, main circuit Main
// ULA
module ULA (
  input  [7:0] A,
  input  [7:0] B,
  input  s,
  output F0,
  output A_B,
  output A_B_2,
  output A_B_3,
  output [7:0] R
);

  wire and_1_out, and_2_out, and_3_out, inversor_1_f0, not_1_out, not_2_out, soma8bit_1_f0;
  wire [7:0] inversor_1_r, selecionador_1_r, selecionador_2_r, selecionador_3_r, soma8bit_1_a___b;

  not not_1 (not_1_out, s);
  Selecionador selecionador_1 (.B(B), .R(selecionador_1_r), .S(not_1_out));
  Soma8bit soma8bit_1 (.C0(not_2_out), .A(A), .B(B), .A___B(soma8bit_1_a___b), .F0(soma8bit_1_f0));  // open: Cout
  not not_2 (not_2_out, not_1_out);
  and and_1 (and_1_out, not_1_out, not_2_out);
  Selecionador selecionador_2 (.B(soma8bit_1_a___b), .R(selecionador_2_r), .S(not_2_out));
  Inversor inversor_1 (.R(inversor_1_r), .B(selecionador_1_r), .A(A), .F0(inversor_1_f0));  // open: Cout
  Soma8bit soma8bit_2 (.C0(and_1_out), .A(selecionador_2_r), .B(selecionador_3_r), .A___B(R));  // open: F0, Cout
  and and_2 (and_2_out, inversor_1_f0, s);
  Selecionador selecionador_3 (.B(inversor_1_r), .R(selecionador_3_r), .S(not_1_out));
  and and_3 (and_3_out, soma8bit_1_f0, not_1_out);
  or or_1 (F0, and_2_out, and_3_out);
  Comp8bit comp8bit_1 (.A(A), .B(B), .A___B(A_B), .A___B_2(A_B_2), .A___B_3(A_B_3));
endmodule

// S1bit
module Soma1bit (
  input  A,
  input  B,
  input  Cin,
  output Cout,
  output S
);

  wire and_1_out, and_2_out, xor_1_out;

  xor xor_1 (xor_1_out, B, A);
  and and_1 (and_1_out, B, A);
  and and_2 (and_2_out, Cin, xor_1_out);
  or or_1 (Cout, and_1_out, and_2_out);
  xor xor_2 (S, xor_1_out, Cin);
endmodule

// Soma
module Soma8bit (
  input  [7:0] A,
  input  [7:0] B,
  input  C0,
  output Cout,
  output [7:0] A___B,
  output F0
);

  wire and_1_out, and_2_out, not_1_out, not_2_out, soma1bit_1_cout, soma1bit_2_cout, soma1bit_3_cout,
       soma1bit_4_cout, soma1bit_5_cout, soma1bit_6_cout, soma1bit_7_cout;

  Soma1bit soma1bit_1 (.Cin(C0), .A(A[0]), .B(B[0]), .Cout(soma1bit_1_cout), .S(A___B[0]));
  Soma1bit soma1bit_2 (.Cin(soma1bit_1_cout), .A(A[1]), .B(B[1]), .Cout(soma1bit_2_cout), .S(A___B[1]));
  Soma1bit soma1bit_3 (.Cin(soma1bit_2_cout), .A(A[2]), .B(B[2]), .Cout(soma1bit_3_cout), .S(A___B[2]));
  Soma1bit soma1bit_4 (.Cin(soma1bit_3_cout), .A(A[3]), .B(B[3]), .Cout(soma1bit_4_cout), .S(A___B[3]));
  Soma1bit soma1bit_5 (.Cin(soma1bit_4_cout), .A(A[4]), .B(B[4]), .Cout(soma1bit_5_cout), .S(A___B[4]));
  or or_1 (F0, and_1_out, and_2_out);
  Soma1bit soma1bit_6 (.Cin(soma1bit_5_cout), .A(A[5]), .B(B[5]), .Cout(soma1bit_6_cout), .S(A___B[5]));
  Soma1bit soma1bit_7 (.Cin(soma1bit_6_cout), .A(A[6]), .B(B[6]), .Cout(soma1bit_7_cout), .S(A___B[6]));
  not not_1 (not_1_out, soma1bit_7_cout);
  and and_1 (and_1_out, Cout, not_1_out);
  Soma1bit soma1bit_8 (.Cin(soma1bit_7_cout), .A(A[7]), .B(B[7]), .Cout(Cout), .S(A___B[7]));
  not not_2 (not_2_out, Cout);
  and and_2 (and_2_out, soma1bit_7_cout, not_2_out);
endmodule

// C1
module Comp1Bit (
  input  A,
  input  B,
  output A___B,
  output A___B_2,
  output A___B_3
);

  wire and_2_out, and_3_out, not_1_out, not_2_out, not_3_out, not_4_out;

  not not_1 (not_1_out, B);
  not not_2 (not_2_out, A);
  not not_3 (not_3_out, B);
  not not_4 (not_4_out, A);
  and and_1 (A___B, A, not_1_out);
  and and_2 (and_2_out, A, B);
  and and_3 (and_3_out, not_2_out, not_3_out);
  and and_4 (A___B_3, not_4_out, B);
  or or_1 (A___B_2, and_2_out, and_3_out);
endmodule

// C2
module Comp2bit (
  input  [1:0] A,
  input  [1:0] B,
  output out_3,
  output out_4,
  output out_5
);

  wire and_1_out, and_2_out, comp1bit_1_a___b, comp1bit_1_a___b_2, comp1bit_1_a___b_3, comp1bit_2_a___b,
       comp1bit_2_a___b_2, comp1bit_2_a___b_3;

  Comp1Bit comp1bit_1 (
    .A(A[1]), .B(B[1]), .A___B(comp1bit_1_a___b), .A___B_2(comp1bit_1_a___b_2), .A___B_3(comp1bit_1_a___b_3));
  Comp1Bit comp1bit_2 (
    .A(A[0]), .B(B[0]), .A___B(comp1bit_2_a___b), .A___B_2(comp1bit_2_a___b_2), .A___B_3(comp1bit_2_a___b_3));
  and and_1 (and_1_out, comp1bit_1_a___b_2, comp1bit_2_a___b);
  and and_2 (and_2_out, comp1bit_1_a___b_2, comp1bit_2_a___b_3);
  or or_1 (out_3, comp1bit_1_a___b, and_1_out);
  and and_3 (out_4, comp1bit_1_a___b_2, comp1bit_2_a___b_2);
  or or_2 (out_5, and_2_out, comp1bit_1_a___b_3);
endmodule

module Comp4bit (
  input  [3:0] A,
  input  [3:0] B,
  output A___B,
  output A___B_2,
  output A___B_3
);

  wire and_1_out, and_2_out, comp2bit_1_out_3, comp2bit_1_out_4, comp2bit_1_out_5, comp2bit_2_out_3,
       comp2bit_2_out_4, comp2bit_2_out_5;

  Comp2bit comp2bit_1 (
    .A(A[3:2]), .B(B[3:2]), .out_3(comp2bit_1_out_3), .out_4(comp2bit_1_out_4), .out_5(comp2bit_1_out_5));
  Comp2bit comp2bit_2 (
    .A(A[1:0]), .B(B[1:0]), .out_3(comp2bit_2_out_3), .out_4(comp2bit_2_out_4), .out_5(comp2bit_2_out_5));
  and and_1 (and_1_out, comp2bit_1_out_4, comp2bit_2_out_3);
  and and_2 (and_2_out, comp2bit_1_out_4, comp2bit_2_out_5);
  or or_1 (A___B, comp2bit_1_out_3, and_1_out);
  and and_3 (A___B_2, comp2bit_1_out_4, comp2bit_2_out_4);
  or or_2 (A___B_3, comp2bit_1_out_5, and_2_out);
endmodule

// Comparador
module Comp8bit (
  input  [7:0] A,
  input  [7:0] B,
  output A___B,
  output A___B_2,
  output A___B_3
);

  wire and_1_out, and_2_out, comp4bit_1_a___b, comp4bit_1_a___b_2, comp4bit_1_a___b_3, comp4bit_2_a___b,
       comp4bit_2_a___b_2, comp4bit_2_a___b_3;

  Comp4bit comp4bit_1 (
    .A(A[7:4]), .B(B[7:4]), .A___B(comp4bit_1_a___b), .A___B_2(comp4bit_1_a___b_2),
    .A___B_3(comp4bit_1_a___b_3));
  Comp4bit comp4bit_2 (
    .A(A[3:0]), .B(B[3:0]), .A___B(comp4bit_2_a___b), .A___B_2(comp4bit_2_a___b_2),
    .A___B_3(comp4bit_2_a___b_3));
  and and_1 (and_1_out, comp4bit_1_a___b_2, comp4bit_2_a___b);
  and and_2 (and_2_out, comp4bit_1_a___b_2, comp4bit_2_a___b_3);
  or or_1 (A___B, comp4bit_1_a___b, and_1_out);
  and and_3 (A___B_2, comp4bit_1_a___b_2, comp4bit_2_a___b_2);
  or or_2 (A___B_3, comp4bit_1_a___b_3, and_2_out);
endmodule

module Selecionador (
  input  [7:0] B,
  input  S,
  output [7:0] R
);

  wire _0_2_out, _0_out, _1_2_out, _1_out, _2_2_out, _2_out, _3_2_out, _3_out, _4_2_out, _4_out, _5_2_out,
       _5_out, _6_2_out, _6_out, _7_2_out, _7_out, not_1_out, not_2_out, not_3_out, not_4_out, not_5_out,
       not_6_out, not_7_out, not_8_out;
  wire [7:0] Inverspr_r;

  Inversor Inverspr (.R(Inverspr_r), .B(B), .A(B));  // open: Cout, F0
  and _0 (_0_out, B[0], not_1_out);
  not not_1 (not_1_out, S);
  and _1 (_1_out, B[1], not_2_out);
  not not_2 (not_2_out, S);
  and _2 (_2_out, B[2], not_3_out);
  not not_3 (not_3_out, S);
  and _3 (_3_out, B[3], not_4_out);
  not not_4 (not_4_out, S);
  and _4 (_4_out, B[4], not_5_out);
  not not_5 (not_5_out, S);
  and _5 (_5_out, B[5], not_6_out);
  not not_6 (not_6_out, S);
  and _6 (_6_out, B[6], not_7_out);
  not not_7 (not_7_out, S);
  and _7 (_7_out, B[7], not_8_out);
  not not_8 (not_8_out, S);
  and _0_2 (_0_2_out, Inverspr_r[0], S);
  and _1_2 (_1_2_out, Inverspr_r[1], S);
  and _2_2 (_2_2_out, Inverspr_r[2], S);
  and _3_2 (_3_2_out, Inverspr_r[3], S);
  and _4_2 (_4_2_out, Inverspr_r[4], S);
  and _5_2 (_5_2_out, Inverspr_r[5], S);
  and _6_2 (_6_2_out, Inverspr_r[6], S);
  and _7_2 (_7_2_out, Inverspr_r[7], S);
  or _0_3 (R[0], _0_out, _0_2_out);
  or _1_3 (R[1], _1_out, _1_2_out);
  or _2_3 (R[2], _2_out, _2_2_out);
  or _3_3 (R[3], _3_out, _3_2_out);
  or _4_3 (R[4], _4_out, _4_2_out);
  or _5_3 (R[5], _5_out, _5_2_out);
  or _6_3 (R[6], _6_out, _6_2_out);
  or _7_3 (R[7], _7_out, _7_2_out);
endmodule

module Inversor (
  input  [7:0] A,
  input  [7:0] B,
  output F0,
  output Cout,
  output [7:0] R
);

  wire [7:0] not_1_out;

  not not_1 (not_1_out[0], B[0]);
  not not_2 (not_1_out[1], B[1]);
  not not_3 (not_1_out[2], B[2]);
  not not_4 (not_1_out[3], B[3]);
  not not_5 (not_1_out[4], B[4]);
  not not_6 (not_1_out[5], B[5]);
  not not_7 (not_1_out[6], B[6]);
  not not_8 (not_1_out[7], B[7]);
  Soma8bit soma8bit_1 (.C0(1'b1), .A(A), .B(not_1_out), .A___B(R), .F0(F0), .Cout(Cout));
endmodule

module Main (
  input  [7:0] A,
  input  [7:0] B,
  input  S,
  output A_B,
  output A_B_2,
  output A_B_3,
  output Overflow,
  output [7:0] Resultado
);

  ULA ula_1 (.A(A), .B(B), .s(S), .R(Resultado), .F0(Overflow), .A_B(A_B), .A_B_2(A_B_2), .A_B_3(A_B_3));
endmodule
